// Logisim project CS_173_evaluation_1_template - Copy (3).circ as structural Verilog: 15 circuits, main circuit StudentSolution
module Exam (
);

  wire Alarm_out, clock_1_out, Left_out, Mres_out, Right_out, Solution_l0, Solution_l1, Solution_l2,
       Solution_l3, Solution_l4, Solution_r0, Solution_r1, Solution_r2, Solution_r3, Solution_r4;

  Button Mres (.out(Mres_out));
  Clock clock_1 (.out(clock_1_out));
  DotMatrix #(.matrixrows(1)) LampsLeft (
    .col0(Solution_l4), .col1(Solution_l3), .col2(Solution_l2), .col3(Solution_l1), .col4(Solution_l0));
  Button Left (.out(Left_out));
  DotMatrix #(.matrixrows(1)) LampsRight (
    .col0(Solution_r4), .col1(Solution_r3), .col2(Solution_r2), .col3(Solution_r1), .col4(Solution_r0));
  Button Alarm (.out(Alarm_out));
  Button Right (.out(Right_out));
  StudentSolution Solution (
    .L2(Solution_l2), .L3(Solution_l3), .L4(Solution_l4), .L0(Solution_l0), .L1(Solution_l1),
    .R2(Solution_r2), .R3(Solution_r3), .R4(Solution_r4), .R0(Solution_r0), .R1(Solution_r1),
    .Clock(clock_1_out), .Left(Left_out), .Right(Right_out), .Alarm(Alarm_out), .Reset(Mres_out));

  // Notes on the sheet:
  //   Do not modify this sheet
endmodule

module StudentSolution (
  input  Reset,
  input  Clock,
  input  Left,
  input  Right,
  input  Alarm,
  output L0,
  output R0,
  output L1,
  output R1,
  output L2,
  output R2,
  output L3,
  output R3,
  output L4,
  output R4
);

  wire e3solution_1_butout, e3solution_2_butout, or_1_out, or_2_out;
  wire [3:0] e3solution_1_state;

  E3Solution e3solution_1 (
    .Butin(Left), .Clock(Clock), .Reset(Reset), .State(e3solution_1_state), .Butout(e3solution_1_butout));
  E3Solution e3solution_2 (.Butin(Right), .Clock(Clock), .Reset(Reset), .Butout(e3solution_2_butout));  // open: State
  or or_1 (or_1_out, e3solution_1_butout, Alarm);
  or or_2 (or_2_out, Alarm, e3solution_2_butout);
  E1Solution e1solution_1 (.Activate(or_1_out), .Clock(Clock), .Lamps({L4, L3, L2, L1, L0}));  // open: Reset
  E1Solution e1solution_2 (.Activate(or_2_out), .Clock(Clock), .Lamps({R4, R3, R2, R1, R0}));  // open: Reset

  // Other names for the same wires on the sheet: AlarmButton = Alarm; LeftButton = Left;
  //   LeftLamps[4:0] = {L4, L3, L2, L1, L0}; RightButton = Right; RightLamps[4:0] = {R4, R3, R2, R1, R0}

  // Notes on the sheet:
  //   Put your solution below. Do not modify or move the components above; use tunnels to connect to them
endmodule

module E1Solution (
  input  Reset,
  input  Activate,
  input  Clock,
  output [4:0] Lamps
);

  E1_Medvedev_FSM e1_medvedev_fsm_1 (.Activate(Activate), .Clck(Clock), .Q(Lamps));

  // Notes on the sheet:
  //   Put your solution below. Do not modify or move the components above; use tunnels to connect to them
endmodule

module E3Solution (
  input  Butin,
  input  Clock,
  input  Reset,
  output [3:0] State,
  output Butout
);

  wire [3:0] e3_nextstate_1_d, register_1_q;

  E3_nextState e3_nextstate_1 (.ButIn(Butin), .C(State), .D(e3_nextstate_1_d), .ButOut(Butout));
  Register #(.width(4)) register_1 (.D(e3_nextstate_1_d), .clk(Clock), .Q(register_1_q));  // open: en, clr
  if_4 if_4_1 (.A(4'b0001), .condition(Reset), .B(register_1_q), .out_4(State));

  // Notes on the sheet:
  //   Put your solution below. Do not modify or move the components above; use tunnels to connect to them
endmodule

module E5Solution (
  input  button,
  input  clock,
  input  Reset,
  output short,
  output [3:0] state
);


  // Notes on the sheet:
  //   Put your solution below. Do not modify or move the components above; use tunnels to connect to them
endmodule

module slatch (
  input  R,
  input  S,
  input  POR,
  output Q
);

  wire nor_2_out, or_1_out;

  nor nor_1 (Q, R, or_1_out);
  or or_1 (or_1_out, POR, nor_2_out);
  nor nor_2 (nor_2_out, Q, S);
endmodule

module E1_nextState (
  input  [4:0] C,
  input  Act,
  output [4:0] D
);

  wire and_1_out, and_2_out, not_1_out;

  not not_1 (not_1_out, C[4]);
  and and_1 (and_1_out, not_1_out, C[2]);
  and and_2 (and_2_out, Act, not_1_out);
  or or_1 (D[2], and_1_out, and_2_out);

  assign {D[4:3], D[1:0]} = {C[1], {2{C[2]}}, C[1]};
endmodule

module E1_Medvedev_FSM (
  input  Activate,
  input  Clck,
  output [4:0] Q
);

  wire [4:0] e1_nextstate_1_d;

  Register #(.width(5)) FFs (.D(e1_nextstate_1_d), .clk(Clck), .Q(Q));  // open: en, clr
  E1_nextState e1_nextstate_1 (.C(Q), .Act(Activate), .D(e1_nextstate_1_d));
endmodule

module E3_nextState (
  input  ButIn,
  input  [3:0] C,
  output [3:0] D,
  output ButOut
);

  wire and_1_out, and_2_out, and_5_out, and_6_out, and_7_out, and_8_out, and_9_out, and_10_out, not_1_out,
       not_2_out, not_3_out, not_4_out, not_5_out;

  not not_1 (not_1_out, ButIn);
  not not_2 (not_2_out, C[3]);
  not not_3 (not_3_out, C[2]);
  not not_4 (not_4_out, C[1]);
  not not_5 (not_5_out, C[0]);
  and and_1 (and_1_out, ButIn, not_2_out, C[2], not_4_out, not_5_out);
  and and_2 (and_2_out, ButIn, C[3], not_3_out, not_4_out, not_5_out);
  and and_3 (D[2], ButIn, not_2_out, not_3_out, C[1], not_5_out);
  and and_4 (D[1], ButIn, not_2_out, not_4_out, C[0]);
  and and_5 (and_5_out, not_2_out, not_3_out, not_4_out, not_5_out);
  and and_6 (and_6_out, C[1], C[0]);
  and and_7 (and_7_out, C[2], C[1]);
  and and_8 (and_8_out, C[3], C[0]);
  and and_9 (and_9_out, C[3], C[1]);
  and and_10 (and_10_out, C[3], C[2]);
  and and_11 (ButOut, ButIn, C[3], not_3_out, not_4_out, not_5_out);
  or or_1 (D[3], and_1_out, and_2_out);
  or or_2 (D[0], not_1_out, and_5_out, and_6_out, and_7_out, and_8_out, and_9_out, and_10_out);
endmodule

module E5_fsm (
  input  button,
  input  C,
  output D
);


  assign D = button;
endmodule

module t (
  input  in_1
);

  wire d_ff_1_q, e5_fsm_1_d, undriven;

  E5_fsm e5_fsm_1 (.button(in_1), .C(d_ff_1_q), .D(e5_fsm_1_d));
  D_Flip_Flop d_ff_1 (.D(e5_fsm_1_d), .clk(undriven), .Q(d_ff_1_q));  // open: Qn, preset, reset
  // Probe on d_ff_1_q
endmodule

module if_gt (
  input  A,
  input  condition,
  input  B,
  output P
);

  wire and_1_out, and_2_out;

  and and_1 (and_1_out, A, condition);
  and and_2 (and_2_out, ~condition, B);  // AND_Gate
  or or_1 (P, and_1_out, and_2_out);
endmodule

module if_4 (
  input  [3:0] A,
  input  condition,
  input  [3:0] B,
  output [3:0] out_4
);

  wire [3:0] and_1_out, and_2_out;

  assign and_1_out = A & {4{condition}};  // AND_Gate and_1, 4 bits wide
  assign and_2_out = ~{4{condition}} & B;  // AND_Gate and_2, 4 bits wide
  assign out_4 = and_1_out | and_2_out;  // OR_Gate or_1, 4 bits wide
endmodule

module if_5 (
  input  [4:0] A,
  input  condition,
  input  [4:0] B,
  output [4:0] P
);

  wire [4:0] and_1_out, and_2_out;

  assign and_1_out = A & {5{condition}};  // AND_Gate and_1, 5 bits wide
  assign and_2_out = ~{5{condition}} & B;  // AND_Gate and_2, 5 bits wide
  assign P = and_1_out | and_2_out;  // OR_Gate or_1, 5 bits wide
endmodule

module shiftregistr (
  input  D,
  input  Clck,
  input  R,
  output Q0,
  output Q1,
  output Q2,
  output Q3
);

  D_Flip_Flop d_ff_1 (.D(D), .clk(Clck), .Q(Q0), .reset(R));  // open: Qn, preset
  D_Flip_Flop d_ff_2 (.D(Q0), .clk(Clck), .Q(Q1), .reset(R));  // open: Qn, preset
  D_Flip_Flop d_ff_3 (.D(Q1), .clk(Clck), .Q(Q2), .reset(R));  // open: Qn, preset
  D_Flip_Flop d_ff_4 (.D(Q2), .clk(Clck), .Q(Q3), .reset(R));  // open: Qn, preset
endmodule
