// Logisim project CS_173_evaluation_1_template - Copy (4).circ as structural Verilog: 20 circuits, main circuit StudentSolution
module Exam (
);

  wire Alarm_out, clock_1_out, Left_out, Mres_out, Right_out, Solution_l0, Solution_l1, Solution_l2,
       Solution_l3, Solution_l4, Solution_r0, Solution_r1, Solution_r2, Solution_r3, Solution_r4;

  Button Mres (.out(Mres_out));
  Clock clock_1 (.out(clock_1_out));
  DotMatrix #(.matrixrows(1)) LampsLeft (
    .col0(Solution_l4), .col1(Solution_l3), .col2(Solution_l2), .col3(Solution_l1), .col4(Solution_l0));
  Button Left (.out(Left_out));
  DotMatrix #(.matrixrows(1)) LampsRight (
    .col0(Solution_r4), .col1(Solution_r3), .col2(Solution_r2), .col3(Solution_r1), .col4(Solution_r0));
  Button Alarm (.out(Alarm_out));
  Button Right (.out(Right_out));
  StudentSolution Solution (
    .L2(Solution_l2), .L3(Solution_l3), .L4(Solution_l4), .L0(Solution_l0), .L1(Solution_l1),
    .R2(Solution_r2), .R3(Solution_r3), .R4(Solution_r4), .R0(Solution_r0), .R1(Solution_r1),
    .Clock(clock_1_out), .Left(Left_out), .Right(Right_out), .Alarm(Alarm_out), .Reset(Mres_out));

  // Notes on the sheet:
  //   Do not modify this sheet
endmodule

module StudentSolution (
  input  Reset,
  input  Clock,
  input  Left,
  input  Right,
  input  Alarm,
  output L0,
  output R0,
  output L1,
  output R1,
  output L2,
  output R2,
  output L3,
  output R3,
  output L4,
  output R4
);

  wire count24_1_p3, count24_1_p5, count24_1_p6, count24_2_p3, count24_2_p5, count24_2_p6,
       e3solution_1_butout, e3solution_2_butout, e5solution_1_short, e5solution_2_short, or_1_out, or_2_out;

  E3Solution e3solution_1 (.Butin(Left), .Clock(Clock), .Reset(Reset), .Butout(e3solution_1_butout));  // open: State
  E5Solution e5solution_1 (.button(Left), .clock(Clock), .Reset(Reset), .short(e5solution_1_short));  // open: state
  E3Solution e3solution_2 (.Butin(Right), .Clock(Clock), .Reset(Reset), .Butout(e3solution_2_butout));  // open: State
  E5Solution e5solution_2 (.button(Right), .clock(Clock), .Reset(Reset), .short(e5solution_2_short));  // open: state
  // count24 count24_1: pin names not known; wires that end beside it: e5solution_2_short, Clock, count24_1_p3, Reset, count24_1_p5, count24_1_p6, count24_1_p6, Clock
  // count24 count24_2: pin names not known; wires that end beside it: e5solution_1_short, Clock, count24_2_p3, Reset, count24_2_p5, count24_2_p6, count24_2_p6, Clock
  or or_1 (or_1_out, e3solution_1_butout, count24_2_p5, Alarm);
  or or_2 (or_2_out, Alarm, e3solution_2_butout, count24_1_p5);
  E1Solution e1solution_1 (.Reset(Reset), .Activate(or_1_out), .Clock(Clock), .Lamps({L4, L3, L2, L1, L0}));
  E1Solution e1solution_2 (.Reset(Reset), .Activate(or_2_out), .Clock(Clock), .Lamps({R4, R3, R2, R1, R0}));

  // Other names for the same wires on the sheet: AlarmButton = Alarm; LeftButton = Left;
  //   LeftLamps[4:0] = {L4, L3, L2, L1, L0}; RightButton = Right; RightLamps[4:0] = {R4, R3, R2, R1, R0}

  // Notes on the sheet:
  //   Put your solution below. Do not modify or move the components above; use tunnels to connect to them
endmodule

module E1Solution (
  input  Reset,
  input  Activate,
  input  Clock,
  output [4:0] Lamps
);

  E1_Medvedev_FSM e1_medvedev_fsm_1 (.Activate(Activate), .Clck(Clock), .Reset(Reset), .Q(Lamps));

  // Notes on the sheet:
  //   Put your solution below. Do not modify or move the components above; use tunnels to connect to them
endmodule

module E3Solution (
  input  Butin,
  input  Clock,
  input  Reset,
  output [3:0] State,
  output Butout
);

  wire [3:0] e3_nextstate_1_d, register_1_q;

  E3_nextState e3_nextstate_1 (.ButIn(Butin), .C(State), .D(e3_nextstate_1_d), .ButOut(Butout));
  Register #(.width(4)) register_1 (.D(e3_nextstate_1_d), .clk(Clock), .Q(register_1_q));  // open: en, clr
  if_4 if_4_1 (.A(4'b0001), .condition(Reset), .B(register_1_q), .out_4(State));

  // Notes on the sheet:
  //   Put your solution below. Do not modify or move the components above; use tunnels to connect to them
endmodule

module E5Solution (
  input  button,
  input  clock,
  input  Reset,
  output short,
  output [3:0] state
);

  wire and_1_out, e5_fsm_1_q;

  E5_FSM e5_fsm_1 (.Button(button), .Clck(clock), .Q(e5_fsm_1_q));
  shiftregistr shiftregistr_1 (
    .D(e5_fsm_1_q), .R(Reset), .Clck(clock), .Q0(state[0]), .Q1(state[1]), .Q2(state[2]), .Q3(state[3]));
  and and_1 (and_1_out, state[2], ~state[3]);  // AND_Gate
  and and_2 (short, ~button, and_1_out);  // AND_Gate

  // Notes on the sheet:
  //   Put your solution below. Do not modify or move the components above; use tunnels to connect to them
endmodule

module E1_nextState (
  input  [4:0] C,
  input  Act,
  output [4:0] D
);

  wire and_1_out, and_2_out, not_1_out;

  not not_1 (not_1_out, C[4]);
  and and_1 (and_1_out, not_1_out, C[2]);
  and and_2 (and_2_out, Act, not_1_out);
  or or_1 (D[2], and_1_out, and_2_out);

  assign {D[4:3], D[1:0]} = {C[1], {2{C[2]}}, C[1]};
endmodule

module E1_Medvedev_FSM (
  input  Activate,
  input  Clck,
  input  Reset,
  output [4:0] Q
);

  wire [4:0] e1_nextstate_1_d, if_5_1_p;

  if_5 if_5_1 (.A({5{1'b0}}), .condition(Reset), .B(Q), .P(if_5_1_p));
  E1_nextState e1_nextstate_1 (.C(if_5_1_p), .Act(Activate), .D(e1_nextstate_1_d));
  Register #(.width(5)) FFs (.D(e1_nextstate_1_d), .clk(Clck), .Q(Q));  // open: en, clr
endmodule

module E3_nextState (
  input  ButIn,
  input  [3:0] C,
  output [3:0] D,
  output ButOut
);

  wire and_1_out, and_2_out, and_5_out, and_6_out, and_7_out, and_8_out, and_9_out, and_10_out, not_1_out,
       not_2_out, not_3_out, not_4_out, not_5_out;

  not not_1 (not_1_out, ButIn);
  not not_2 (not_2_out, C[3]);
  not not_3 (not_3_out, C[2]);
  not not_4 (not_4_out, C[1]);
  not not_5 (not_5_out, C[0]);
  and and_1 (and_1_out, ButIn, not_2_out, C[2], not_4_out, not_5_out);
  and and_2 (and_2_out, ButIn, C[3], not_3_out, not_4_out, not_5_out);
  and and_3 (D[2], ButIn, not_2_out, not_3_out, C[1], not_5_out);
  and and_4 (D[1], ButIn, not_2_out, not_4_out, C[0]);
  and and_5 (and_5_out, not_2_out, not_3_out, not_4_out, not_5_out);
  and and_6 (and_6_out, C[1], C[0]);
  and and_7 (and_7_out, C[2], C[1]);
  and and_8 (and_8_out, C[3], C[0]);
  and and_9 (and_9_out, C[3], C[1]);
  and and_10 (and_10_out, C[3], C[2]);
  and and_11 (ButOut, ButIn, C[3], not_3_out, not_4_out, not_5_out);
  or or_1 (D[3], and_1_out, and_2_out);
  or or_2 (D[0], not_1_out, and_5_out, and_6_out, and_7_out, and_8_out, and_9_out, and_10_out);
endmodule

module E5_FSM (
  input  Button,
  input  Clck,
  output Q
);

  D_Flip_Flop d_ff_1 (.D(Button), .clk(Clck), .Q(Q), .preset(Button));  // open: Qn, reset
endmodule

module if_gt (
  input  A,
  input  condition,
  input  B,
  output P
);

  wire and_1_out, and_2_out;

  and and_1 (and_1_out, A, condition);
  and and_2 (and_2_out, ~condition, B);  // AND_Gate
  or or_1 (P, and_1_out, and_2_out);
endmodule

module if_4 (
  input  [3:0] A,
  input  condition,
  input  [3:0] B,
  output [3:0] out_4
);

  wire [3:0] and_1_out, and_2_out;

  assign and_1_out = A & {4{condition}};  // AND_Gate and_1, 4 bits wide
  assign and_2_out = ~{4{condition}} & B;  // AND_Gate and_2, 4 bits wide
  assign out_4 = and_1_out | and_2_out;  // OR_Gate or_1, 4 bits wide
endmodule

module if_5 (
  input  [4:0] A,
  input  condition,
  input  [4:0] B,
  output [4:0] P
);

  wire [4:0] and_1_out, and_2_out;

  assign and_1_out = A & {5{condition}};  // AND_Gate and_1, 5 bits wide
  assign and_2_out = ~{5{condition}} & B;  // AND_Gate and_2, 5 bits wide
  assign P = and_1_out | and_2_out;  // OR_Gate or_1, 5 bits wide
endmodule

module shiftregistr (
  input  D,
  input  R,
  input  Clck,
  output Q0,
  output Q1,
  output Q2,
  output Q3
);

  D_Flip_Flop d_ff_1 (.D(D), .clk(Clck), .Q(Q0), .reset(R));  // open: Qn, preset
  D_Flip_Flop d_ff_2 (.D(Q0), .clk(Clck), .Q(Q1), .reset(R));  // open: Qn, preset
  D_Flip_Flop d_ff_3 (.D(Q1), .clk(Clck), .Q(Q2), .reset(R));  // open: Qn, preset
  D_Flip_Flop d_ff_4 (.D(Q2), .clk(Clck), .Q(Q3), .reset(R));  // open: Qn, preset
endmodule

module slatch (
  input  R,
  input  S,
  input  POR,
  output Q
);

  wire nor_2_out, or_1_out;

  nor nor_1 (Q, R, or_1_out);
  or or_1 (or_1_out, POR, nor_2_out);
  nor nor_2 (nor_2_out, Q, S);
endmodule

module fsm6 (
  input  Activate,
  input  Clck,
  input  Reset,
  input  POR,
  output [2:0] D,
  output Ended,
  output active
);

  wire [2:0] countto6_1_d;

  slatch slatch_1 (.R(Reset), .S(Activate), .POR(POR), .Q(active));
  countTo6 countto6_1 (.E(active), .C(D), .D(countto6_1_d), .Ended(Ended));
  Register #(.width(3)) register_1 (.D(countto6_1_d), .clk(Clck), .Q(D), .clr(Reset));  // open: en
  // Probe on D
endmodule

module countTo3 (
  input  R,
  input  Act,
  input  POR,
  input  [1:0] C,
  output [1:0] D,
  output Ended
);

  wire and_1_out, and_2_out, and_3_out, and_4_out, and_5_out, and_6_out, and_7_out, not_1_out, not_2_out,
       not_3_out, slatch_1_q;

  slatch slatch_1 (.R(R), .S(Act), .POR(POR), .Q(slatch_1_q));
  not not_1 (not_1_out, slatch_1_q);
  not not_2 (not_2_out, R);
  not not_3 (not_3_out, C[0]);
  and and_1 (and_1_out, not_2_out, C[1]);
  and and_2 (and_2_out, slatch_1_q, not_2_out, C[0]);
  and and_3 (and_3_out, not_1_out, not_2_out, C[0]);
  and and_4 (and_4_out, slatch_1_q, not_2_out, not_3_out);
  and and_5 (and_5_out, slatch_1_q, not_2_out, C[1]);
  and and_6 (and_6_out, not_2_out, C[1], C[0]);
  and and_7 (and_7_out, slatch_1_q, not_2_out, C[1]);
  or or_1 (D[1], and_1_out, and_2_out);
  or or_2 (D[0], and_3_out, and_4_out, and_5_out);
  or or_3 (Ended, and_6_out, and_7_out);
endmodule

module countTo6 (
  input  E,
  input  [2:0] C,
  output [2:0] D,
  output Ended
);

  wire and_1_out, and_2_out, and_3_out, and_4_out, and_5_out, and_6_out, and_7_out, and_8_out, not_1_out,
       not_2_out, not_3_out, not_4_out;

  not not_1 (not_1_out, E);
  not not_2 (not_2_out, C[2]);
  not not_3 (not_3_out, C[1]);
  not not_4 (not_4_out, C[0]);
  and and_1 (and_1_out, not_1_out, C[2]);
  and and_2 (and_2_out, C[2], not_3_out);
  and and_3 (and_3_out, E, not_2_out, C[1], C[0]);
  and and_4 (and_4_out, not_1_out, C[1]);
  and and_5 (and_5_out, not_2_out, C[1], not_4_out);
  and and_6 (and_6_out, E, not_3_out, C[0]);
  and and_7 (and_7_out, not_1_out, C[0]);
  and and_8 (and_8_out, E, not_4_out);
  and and_9 (Ended, E, C[2], not_3_out, C[0]);
  or or_1 (D[2], and_1_out, and_2_out, and_3_out);
  or or_2 (D[1], and_4_out, and_5_out, and_6_out);
  or or_3 (D[0], and_7_out, and_8_out);
endmodule

module count24 (
  input  A,
  input  Clck,
  input  POR,
  output seqActive
);

  wire and_2_out, d_ff_1_q, fsm6_1_active, fsm6_1_ended, not_1_out, resetVal;
  wire [2:0] counterto4_1_out_4, fsm6_1_d;

  fsm6 fsm6_1 (
    .Activate(A), .Clck(Clck), .Reset(resetVal), .POR(POR), .D(fsm6_1_d), .Ended(fsm6_1_ended),
    .active(fsm6_1_active));
  // Probe on fsm6_1_d
  counterTo4 counterto4_1 (.Activate(fsm6_1_ended), .Clck(Clck), .Reset(resetVal), .out_4(counterto4_1_out_4));
  // Probe on counterto4_1_out_4
  not not_1 (not_1_out, counterto4_1_out_4[2]);
  and and_1 (seqActive, fsm6_1_active, not_1_out);
  D_Flip_Flop d_ff_1 (.D(and_2_out), .clk(Clck), .Q(d_ff_1_q));  // open: Qn, preset, reset
  and and_2 (and_2_out, fsm6_1_active, counterto4_1_out_4[2]);
  D_Flip_Flop d_ff_2 (.D(d_ff_1_q), .clk(Clck), .Q(resetVal));  // open: Qn, preset, reset
endmodule

module countTo4 (
  input  Enable,
  input  [2:0] C,
  output [2:0] D
);

  wire and_1_out, and_2_out, and_3_out, and_4_out, and_5_out, and_6_out, and_7_out, and_8_out, and_9_out,
       not_1_out, not_2_out, not_3_out, not_4_out;

  not not_1 (not_1_out, Enable);
  not not_2 (not_2_out, C[2]);
  not not_3 (not_3_out, C[1]);
  not not_4 (not_4_out, C[0]);
  and and_1 (and_1_out, not_1_out, C[2], not_3_out, not_4_out);
  and and_2 (and_2_out, Enable, not_2_out, C[1], C[0]);
  and and_3 (and_3_out, not_1_out, not_2_out, C[1]);
  and and_4 (and_4_out, not_2_out, C[1], not_4_out);
  and and_5 (and_5_out, Enable, not_2_out, not_3_out, C[0]);
  and and_6 (and_6_out, not_1_out, not_2_out, C[0]);
  and and_7 (and_7_out, Enable, not_2_out, not_4_out);
  and and_8 (and_8_out, Enable, not_3_out, not_4_out);
  and and_9 (and_9_out, Enable, C[2], not_3_out, not_4_out);
  or or_1 (D[2], and_1_out, and_2_out);
  or or_2 (D[1], and_3_out, and_4_out, and_5_out);
  or or_3 (D[0], and_6_out, and_7_out, and_8_out);
endmodule

module counterTo4 (
  input  Activate,
  input  Clck,
  input  Reset,
  output [2:0] out_4
);

  wire [2:0] countto4_1_d;

  countTo4 countto4_1 (.Enable(Activate), .C(out_4), .D(countto4_1_d));
  Register #(.width(3)) register_1 (.D(countto4_1_d), .clk(Clck), .Q(out_4), .clr(Reset));  // open: en
endmodule
