// Logisim project tp1.3.circ as structural Verilog: 1 circuit, main circuit main
module main (
  input  W,
  input  X,
  input  Y,
  input  Z
);

  wire and_1_out, and_2_out, and_3_out, not_1_out, not_2_out, not_3_out, not_4_out;

  not not_1 (not_1_out, W);
  not not_2 (not_2_out, X);
  not not_3 (not_3_out, Y);
  not not_4 (not_4_out, Z);
  and and_1 (and_1_out, not_1_out, not_2_out);
  and and_2 (and_2_out, not_3_out, not_1_out);
  and and_3 (and_3_out, not_2_out, W, not_4_out, Y);
  // OR_Gate Q has open pins: in0=and_1_out, in1=and_2_out, in2=and_3_out, in3=Z, out=open
endmodule
