// Logisim project tp34.circ as structural Verilog: 5 circuits, main circuit TP34
module TP34 (
);

  wire But_out, clk_out, reset_out, StudentSol_disp0a, StudentSol_disp0b, StudentSol_disp0c,
       StudentSol_disp0d, StudentSol_disp0e, StudentSol_disp0f, StudentSol_disp0g, StudentSol_disp0point,
       StudentSol_disp1a, StudentSol_disp1b, StudentSol_disp1c, StudentSol_disp1d, StudentSol_disp1e,
       StudentSol_disp1f, StudentSol_disp1g, StudentSol_disp1point, StudentSol_disp2a, StudentSol_disp2b,
       StudentSol_disp2c, StudentSol_disp2d, StudentSol_disp2e, StudentSol_disp2f, StudentSol_disp2g,
       StudentSol_disp2point, StudentSol_q00, StudentSol_q01, StudentSol_q02, StudentSol_q10, StudentSol_q11,
       StudentSol_q12, StudentSol_q20, StudentSol_q21, StudentSol_q22;

  Button But (.out(But_out));
  Clock clk (.out(clk_out));
  Button reset (.out(reset_out));
  _7_Segment_Display Disp2 (
    .g(StudentSol_disp2g), .f(StudentSol_disp2f), .a(StudentSol_disp2a), .b(StudentSol_disp2b),
    .e(StudentSol_disp2e), .d(StudentSol_disp2d), .c(StudentSol_disp2c), .dp(StudentSol_disp2point));
  _7_Segment_Display Disp1 (
    .g(StudentSol_disp1g), .f(StudentSol_disp1f), .a(StudentSol_disp1a), .b(StudentSol_disp1b),
    .e(StudentSol_disp1e), .d(StudentSol_disp1d), .c(StudentSol_disp1c), .dp(StudentSol_disp1point));
  LED Q22 (.in(StudentSol_q22));
  LED Q12 (.in(StudentSol_q12));
  LED Q02 (.in(StudentSol_q02));
  _7_Segment_Display Disp0 (
    .g(StudentSol_disp0g), .f(StudentSol_disp0f), .a(StudentSol_disp0a), .b(StudentSol_disp0b),
    .e(StudentSol_disp0e), .d(StudentSol_disp0d), .c(StudentSol_disp0c), .dp(StudentSol_disp0point));
  LED Q21 (.in(StudentSol_q21));
  LED Q20 (.in(StudentSol_q20));
  LED Q11 (.in(StudentSol_q11));
  LED Q10 (.in(StudentSol_q10));
  LED Q01 (.in(StudentSol_q01));
  LED Q00 (.in(StudentSol_q00));
  TP34_StudentSolution StudentSol (
    .Disp0D(StudentSol_disp0d), .Disp0E(StudentSol_disp0e), .Disp0F(StudentSol_disp0f),
    .Disp0G(StudentSol_disp0g), .Disp0Point(StudentSol_disp0point), .Q00(StudentSol_q00),
    .Q01(StudentSol_q01), .Q02(StudentSol_q02), .Disp0A(StudentSol_disp0a), .Disp0B(StudentSol_disp0b),
    .Disp0C(StudentSol_disp0c), .Disp1D(StudentSol_disp1d), .Disp1E(StudentSol_disp1e),
    .Disp1F(StudentSol_disp1f), .Disp1G(StudentSol_disp1g), .Disp1Point(StudentSol_disp1point),
    .Q10(StudentSol_q10), .Q11(StudentSol_q11), .Q12(StudentSol_q12), .Disp1A(StudentSol_disp1a),
    .Disp1B(StudentSol_disp1b), .Disp1C(StudentSol_disp1c), .Disp2D(StudentSol_disp2d),
    .Disp2E(StudentSol_disp2e), .Disp2F(StudentSol_disp2f), .Disp2G(StudentSol_disp2g),
    .Disp2Point(StudentSol_disp2point), .Q20(StudentSol_q20), .Q21(StudentSol_q21), .Q22(StudentSol_q22),
    .Disp2A(StudentSol_disp2a), .Disp2B(StudentSol_disp2b), .Disp2C(StudentSol_disp2c), .res(reset_out),
    .But(But_out), .clk(clk_out));
endmodule

module TP34_StudentSolution (
  input  But,
  input  clk,
  input  res,
  output Disp0A,
  output Disp1A,
  output Disp2A,
  output Disp0B,
  output Disp1B,
  output Disp2B,
  output Disp0C,
  output Disp1C,
  output Disp2C,
  output Disp0D,
  output Disp1D,
  output Disp2D,
  output Disp0E,
  output Disp1E,
  output Disp2E,
  output Disp0F,
  output Disp1F,
  output Disp2F,
  output Disp0G,
  output Disp1G,
  output Disp2G,
  output Disp0Point,
  output Disp1Point,
  output Disp2Point,
  output Q00,
  output Q10,
  output Q20,
  output Q01,
  output Q11,
  output Q21,
  output Q02,
  output Q12,
  output Q22
);


  // Other names for the same wires on the sheet: Button = But; Clock = clk;
  //   Disp0[7:0] = {Disp0Point, Disp0G, Disp0F, Disp0E, Disp0D, Disp0C, Disp0B, Disp0A};
  //   Disp1[7:0] = {Disp1Point, Disp1G, Disp1F, Disp1E, Disp1D, Disp1C, Disp1B, Disp1A};
  //   Disp2[7:0] = {Disp2Point, Disp2G, Disp2F, Disp2E, Disp2D, Disp2C, Disp2B, Disp2A}; Reset = res

  // Notes on the sheet:
  //   Disp0
  //   Q0
  //   Disp1
  //   Q1
  //   Q2
  //   Disp2
endmodule

module TP34Q1Video (
);

  wire clock_1_out, StudentSol_disp0a, StudentSol_disp0b, StudentSol_disp0c, StudentSol_disp0d,
       StudentSol_disp0e, StudentSol_disp0f, StudentSol_disp0g, StudentSol_disp0point, StudentSol_disp1a,
       StudentSol_disp1b, StudentSol_disp1c, StudentSol_disp1d, StudentSol_disp1e, StudentSol_disp1f,
       StudentSol_disp1g, StudentSol_disp1point, StudentSol_disp2a, StudentSol_disp2b, StudentSol_disp2c,
       StudentSol_disp2d, StudentSol_disp2e, StudentSol_disp2f, StudentSol_disp2g, StudentSol_disp2point,
       StudentSol_q00, StudentSol_q01, StudentSol_q02, StudentSol_q10, StudentSol_q11, StudentSol_q12,
       StudentSol_q20, StudentSol_q21, StudentSol_q22, undriven, undriven_2;
  wire [9:0] counter_1_q;

  Clock clock_1 (.out(clock_1_out));
  ROM #(.addrWidth(10), .dataWidth(1)) ROM_But_Q1_sg (.addr(counter_1_q));  // open: data
  Counter #(.max('h187), .width(10)) counter_1 (
    .clr(1'b0), .load(1'b0), .up(1'b1), .count(1'b1), .clk(clock_1_out), .D({10{1'b0}}), .Q(counter_1_q));  // open: carry
  ROM #(.addrWidth(10), .dataWidth(1)) ROM_reset_sg (.addr(counter_1_q));  // open: data
  _7_Segment_Display Disp2 (
    .g(StudentSol_disp2g), .f(StudentSol_disp2f), .a(StudentSol_disp2a), .b(StudentSol_disp2b),
    .e(StudentSol_disp2e), .d(StudentSol_disp2d), .c(StudentSol_disp2c), .dp(StudentSol_disp2point));
  _7_Segment_Display Disp1 (
    .g(StudentSol_disp1g), .f(StudentSol_disp1f), .a(StudentSol_disp1a), .b(StudentSol_disp1b),
    .e(StudentSol_disp1e), .d(StudentSol_disp1d), .c(StudentSol_disp1c), .dp(StudentSol_disp1point));
  LED Q22 (.in(StudentSol_q22));
  LED Q21 (.in(StudentSol_q21));
  LED Q12 (.in(StudentSol_q12));
  LED Q11 (.in(StudentSol_q11));
  LED Q02 (.in(StudentSol_q02));
  LED Q01 (.in(StudentSol_q01));
  _7_Segment_Display Disp0 (
    .g(StudentSol_disp0g), .f(StudentSol_disp0f), .a(StudentSol_disp0a), .b(StudentSol_disp0b),
    .e(StudentSol_disp0e), .d(StudentSol_disp0d), .c(StudentSol_disp0c), .dp(StudentSol_disp0point));
  LED Q20 (.in(StudentSol_q20));
  LED Q10 (.in(StudentSol_q10));
  LED Q00 (.in(StudentSol_q00));
  TP34_StudentSolution StudentSol (
    .Disp0D(StudentSol_disp0d), .Disp0E(StudentSol_disp0e), .Disp0F(StudentSol_disp0f),
    .Disp0G(StudentSol_disp0g), .Disp0Point(StudentSol_disp0point), .Q00(StudentSol_q00),
    .Q01(StudentSol_q01), .Q02(StudentSol_q02), .Disp0A(StudentSol_disp0a), .Disp0B(StudentSol_disp0b),
    .Disp0C(StudentSol_disp0c), .Disp1D(StudentSol_disp1d), .Disp1E(StudentSol_disp1e),
    .Disp1F(StudentSol_disp1f), .Disp1G(StudentSol_disp1g), .Disp1Point(StudentSol_disp1point),
    .Q10(StudentSol_q10), .Q11(StudentSol_q11), .Q12(StudentSol_q12), .Disp1A(StudentSol_disp1a),
    .Disp1B(StudentSol_disp1b), .Disp1C(StudentSol_disp1c), .Disp2D(StudentSol_disp2d),
    .Disp2E(StudentSol_disp2e), .Disp2F(StudentSol_disp2f), .Disp2G(StudentSol_disp2g),
    .Disp2Point(StudentSol_disp2point), .Q20(StudentSol_q20), .Q21(StudentSol_q21), .Q22(StudentSol_q22),
    .Disp2A(StudentSol_disp2a), .Disp2B(StudentSol_disp2b), .Disp2C(StudentSol_disp2c), .res(undriven_2),
    .But(undriven), .clk(clock_1_out));

  // Notes on the sheet:
  //   contents of ROM_reset_sg (hex, n*v repeats v):
  //   5*1
endmodule

module TP34Q2Video (
);

  wire clock_1_out, StudentSol_disp0a, StudentSol_disp0b, StudentSol_disp0c, StudentSol_disp0d,
       StudentSol_disp0e, StudentSol_disp0f, StudentSol_disp0g, StudentSol_disp0point, StudentSol_disp1a,
       StudentSol_disp1b, StudentSol_disp1c, StudentSol_disp1d, StudentSol_disp1e, StudentSol_disp1f,
       StudentSol_disp1g, StudentSol_disp1point, StudentSol_disp2a, StudentSol_disp2b, StudentSol_disp2c,
       StudentSol_disp2d, StudentSol_disp2e, StudentSol_disp2f, StudentSol_disp2g, StudentSol_disp2point,
       StudentSol_q00, StudentSol_q01, StudentSol_q02, StudentSol_q10, StudentSol_q11, StudentSol_q12,
       StudentSol_q20, StudentSol_q21, StudentSol_q22, undriven, undriven_2;
  wire [9:0] counter_1_q;

  Clock clock_1 (.out(clock_1_out));
  ROM #(.addrWidth(10), .dataWidth(1)) ROM_But_Q1_sg (.addr(counter_1_q));  // open: data
  Counter #(.max('h187), .width(10)) counter_1 (
    .clr(1'b0), .load(1'b0), .up(1'b1), .count(1'b1), .clk(clock_1_out), .D({10{1'b0}}), .Q(counter_1_q));  // open: carry
  ROM #(.addrWidth(10), .dataWidth(1)) ROM_reset_sg (.addr(counter_1_q));  // open: data
  _7_Segment_Display Disp2 (
    .g(StudentSol_disp2g), .f(StudentSol_disp2f), .a(StudentSol_disp2a), .b(StudentSol_disp2b),
    .e(StudentSol_disp2e), .d(StudentSol_disp2d), .c(StudentSol_disp2c), .dp(StudentSol_disp2point));
  _7_Segment_Display Disp1 (
    .g(StudentSol_disp1g), .f(StudentSol_disp1f), .a(StudentSol_disp1a), .b(StudentSol_disp1b),
    .e(StudentSol_disp1e), .d(StudentSol_disp1d), .c(StudentSol_disp1c), .dp(StudentSol_disp1point));
  LED Q22 (.in(StudentSol_q22));
  LED Q21 (.in(StudentSol_q21));
  LED Q12 (.in(StudentSol_q12));
  LED Q11 (.in(StudentSol_q11));
  LED Q02 (.in(StudentSol_q02));
  LED Q01 (.in(StudentSol_q01));
  _7_Segment_Display Disp0 (
    .g(StudentSol_disp0g), .f(StudentSol_disp0f), .a(StudentSol_disp0a), .b(StudentSol_disp0b),
    .e(StudentSol_disp0e), .d(StudentSol_disp0d), .c(StudentSol_disp0c), .dp(StudentSol_disp0point));
  LED Q20 (.in(StudentSol_q20));
  LED Q10 (.in(StudentSol_q10));
  LED Q00 (.in(StudentSol_q00));
  TP34_StudentSolution StudentSol (
    .Disp0D(StudentSol_disp0d), .Disp0E(StudentSol_disp0e), .Disp0F(StudentSol_disp0f),
    .Disp0G(StudentSol_disp0g), .Disp0Point(StudentSol_disp0point), .Q00(StudentSol_q00),
    .Q01(StudentSol_q01), .Q02(StudentSol_q02), .Disp0A(StudentSol_disp0a), .Disp0B(StudentSol_disp0b),
    .Disp0C(StudentSol_disp0c), .Disp1D(StudentSol_disp1d), .Disp1E(StudentSol_disp1e),
    .Disp1F(StudentSol_disp1f), .Disp1G(StudentSol_disp1g), .Disp1Point(StudentSol_disp1point),
    .Q10(StudentSol_q10), .Q11(StudentSol_q11), .Q12(StudentSol_q12), .Disp1A(StudentSol_disp1a),
    .Disp1B(StudentSol_disp1b), .Disp1C(StudentSol_disp1c), .Disp2D(StudentSol_disp2d),
    .Disp2E(StudentSol_disp2e), .Disp2F(StudentSol_disp2f), .Disp2G(StudentSol_disp2g),
    .Disp2Point(StudentSol_disp2point), .Q20(StudentSol_q20), .Q21(StudentSol_q21), .Q22(StudentSol_q22),
    .Disp2A(StudentSol_disp2a), .Disp2B(StudentSol_disp2b), .Disp2C(StudentSol_disp2c), .res(undriven_2),
    .But(undriven), .clk(clock_1_out));

  // Notes on the sheet:
  //   contents of ROM_But_Q1_sg (hex, n*v repeats v):
  //   131*0 1 126*0 1
  //   contents of ROM_reset_sg (hex, n*v repeats v):
  //   5*1
endmodule

module TP34Q3Video (
);

  wire clock_1_out, StudentSol_disp0a, StudentSol_disp0b, StudentSol_disp0c, StudentSol_disp0d,
       StudentSol_disp0e, StudentSol_disp0f, StudentSol_disp0g, StudentSol_disp0point, StudentSol_disp1a,
       StudentSol_disp1b, StudentSol_disp1c, StudentSol_disp1d, StudentSol_disp1e, StudentSol_disp1f,
       StudentSol_disp1g, StudentSol_disp1point, StudentSol_disp2a, StudentSol_disp2b, StudentSol_disp2c,
       StudentSol_disp2d, StudentSol_disp2e, StudentSol_disp2f, StudentSol_disp2g, StudentSol_disp2point,
       StudentSol_q00, StudentSol_q01, StudentSol_q02, StudentSol_q10, StudentSol_q11, StudentSol_q12,
       StudentSol_q20, StudentSol_q21, StudentSol_q22, undriven, undriven_2;
  wire [9:0] counter_1_q;

  Clock clock_1 (.out(clock_1_out));
  ROM #(.addrWidth(10), .dataWidth(1)) ROM_But_Q1_sg (.addr(counter_1_q));  // open: data
  Counter #(.max('h187), .width(10)) counter_1 (
    .clr(1'b0), .load(1'b0), .up(1'b1), .count(1'b1), .clk(clock_1_out), .D({10{1'b0}}), .Q(counter_1_q));  // open: carry
  ROM #(.addrWidth(10), .dataWidth(1)) ROM_reset_sg (.addr(counter_1_q));  // open: data
  _7_Segment_Display Disp2 (
    .g(StudentSol_disp2g), .f(StudentSol_disp2f), .a(StudentSol_disp2a), .b(StudentSol_disp2b),
    .e(StudentSol_disp2e), .d(StudentSol_disp2d), .c(StudentSol_disp2c), .dp(StudentSol_disp2point));
  _7_Segment_Display Disp1 (
    .g(StudentSol_disp1g), .f(StudentSol_disp1f), .a(StudentSol_disp1a), .b(StudentSol_disp1b),
    .e(StudentSol_disp1e), .d(StudentSol_disp1d), .c(StudentSol_disp1c), .dp(StudentSol_disp1point));
  LED Q22 (.in(StudentSol_q22));
  LED Q21 (.in(StudentSol_q21));
  LED Q12 (.in(StudentSol_q12));
  LED Q11 (.in(StudentSol_q11));
  LED Q02 (.in(StudentSol_q02));
  LED Q01 (.in(StudentSol_q01));
  _7_Segment_Display Disp0 (
    .g(StudentSol_disp0g), .f(StudentSol_disp0f), .a(StudentSol_disp0a), .b(StudentSol_disp0b),
    .e(StudentSol_disp0e), .d(StudentSol_disp0d), .c(StudentSol_disp0c), .dp(StudentSol_disp0point));
  LED Q20 (.in(StudentSol_q20));
  LED Q10 (.in(StudentSol_q10));
  LED Q00 (.in(StudentSol_q00));
  TP34_StudentSolution StudentSol (
    .Disp0D(StudentSol_disp0d), .Disp0E(StudentSol_disp0e), .Disp0F(StudentSol_disp0f),
    .Disp0G(StudentSol_disp0g), .Disp0Point(StudentSol_disp0point), .Q00(StudentSol_q00),
    .Q01(StudentSol_q01), .Q02(StudentSol_q02), .Disp0A(StudentSol_disp0a), .Disp0B(StudentSol_disp0b),
    .Disp0C(StudentSol_disp0c), .Disp1D(StudentSol_disp1d), .Disp1E(StudentSol_disp1e),
    .Disp1F(StudentSol_disp1f), .Disp1G(StudentSol_disp1g), .Disp1Point(StudentSol_disp1point),
    .Q10(StudentSol_q10), .Q11(StudentSol_q11), .Q12(StudentSol_q12), .Disp1A(StudentSol_disp1a),
    .Disp1B(StudentSol_disp1b), .Disp1C(StudentSol_disp1c), .Disp2D(StudentSol_disp2d),
    .Disp2E(StudentSol_disp2e), .Disp2F(StudentSol_disp2f), .Disp2G(StudentSol_disp2g),
    .Disp2Point(StudentSol_disp2point), .Q20(StudentSol_q20), .Q21(StudentSol_q21), .Q22(StudentSol_q22),
    .Disp2A(StudentSol_disp2a), .Disp2B(StudentSol_disp2b), .Disp2C(StudentSol_disp2c), .res(undriven_2),
    .But(undriven), .clk(clock_1_out));

  // Notes on the sheet:
  //   contents of ROM_But_Q1_sg (hex, n*v repeats v):
  //   131*0 1 126*0 1
  //   contents of ROM_reset_sg (hex, n*v repeats v):
  //   5*1
endmodule
