// Logisim project TP2.1.circ as structural Verilog: 6 circuits, main circuit Main
module Add_0 (
  input  A0,
  input  B0,
  output P0,
  output Co_0
);

  xor xor_1 (P0, A0, B0);
  and and_1 (Co_0, A0, B0);

  // Notes on the sheet:
  //   A0 + B0
  //   Carry out
endmodule

module Add_n (
  input  An,
  input  Bn,
  input  Ci_n,
  output Pn,
  output Co_n
);

  Add_noCarry add_nocarry_1 (.An(An), .Bn(Bn), .Ci_n(Ci_n), .Pn(Pn));
  Carry_out carry_out_1 (.An(An), .Bn(Bn), .Ci_n(Ci_n), .Co_n(Co_n));
endmodule

// 4-Bit Adder
module Main (
  input  A3,
  input  A2,
  input  A1,
  input  A0,
  input  B3,
  input  B2,
  input  B1,
  input  B0,
  output Overflow,
  output P3,
  output P2,
  output P1,
  output P0
);

  wire C1, C2, C3;

  Add_0 Add0 (.A0(A0), .B0(B0), .P0(P0), .Co_0(C1));
  Add_n n_1 (.Pn(P1), .Co_n(C2), .Ci_n(B1), .An(A1), .Bn(C1));
  Add_n n_2 (.Pn(P2), .Co_n(C3), .Ci_n(B2), .An(A2), .Bn(C2));
  Add_n n_3 (.Pn(P3), .Co_n(Overflow), .Ci_n(B3), .An(A3), .Bn(C3));
endmodule

module Answer (
  input  B3,
  input  A3,
  input  B2,
  input  A2,
  input  B1,
  input  A1,
  input  B0,
  input  A0,
  output out_9,
  output out_10,
  output out_11,
  output out_12,
  output Overflow
);

  Main main_1 (
    .A3(A3), .A2(A2), .A1(A1), .A0(A0), .B3(B3), .B2(B2), .B1(B1), .B0(B0), .Overflow(Overflow), .P3(out_9),
    .P2(out_10), .P1(out_11), .P0(out_12));
endmodule

module Carry_out (
  input  An,
  input  Bn,
  input  Ci_n,
  output Co_n
);

  wire and_1_out, and_2_out, or_1_out;

  or or_1 (or_1_out, An, Bn);
  and and_1 (and_1_out, or_1_out, Ci_n);
  and and_2 (and_2_out, An, Bn);
  or or_2 (Co_n, and_1_out, and_2_out);

  // Notes on the sheet:
  //   An+Bn
  //   (An+Bn)*Cn
  //   An*Bn
  //   (An+Bn)*Cn + An*Bn
endmodule

module Add_noCarry (
  input  An,
  input  Bn,
  input  Ci_n,
  output Pn
);

  wire AXORB_out;

  xor AXORB (AXORB_out, An, Bn);
  xor xor_1 (Pn, AXORB_out, Ci_n);

  // Notes on the sheet:
  //   (A XOR B) XOR C
endmodule
