// Logisim project TP2.2.circ as structural Verilog: 5 circuits, main circuit D_Latch
module D_Latch (
  input  D,
  input  E,
  input  POR,
  output Q
);

  wire nand_1_out, nand_2_out, nand_4_out, or_1_out;

  or or_1 (or_1_out, E, POR);
  nand nand_1 (nand_1_out, D, E);
  nand nand_2 (nand_2_out, nand_1_out, or_1_out);
  nand nand_3 (Q, nand_1_out, nand_4_out);
  nand nand_4 (nand_4_out, Q, nand_2_out);
endmodule

module main (
);

  wire and_1_out, and_2_out, and_3_out, and_4_out, and_5_out, and_6_out, button_1_out, lul_out,
       sr_latch_1_out_4, sr_latch_2_out_4, sr_latch_3_out_4;

  Button button_1 (.out(button_1_out));
  Button lul (.out(lul_out));
  and and_1 (and_1_out, sr_latch_1_out_4, sr_latch_2_out_4, sr_latch_3_out_4, ~button_1_out);  // AND_Gate
  and and_2 (and_2_out, ~sr_latch_1_out_4, ~sr_latch_2_out_4, ~sr_latch_3_out_4, button_1_out);  // AND_Gate
  and and_3 (and_3_out, ~sr_latch_1_out_4, sr_latch_2_out_4, sr_latch_3_out_4, button_1_out);  // AND_Gate
  and and_4 (and_4_out, ~sr_latch_2_out_4, ~sr_latch_3_out_4, ~button_1_out, sr_latch_1_out_4);  // AND_Gate
  and and_5 (and_5_out, ~sr_latch_1_out_4, ~sr_latch_2_out_4, ~button_1_out, sr_latch_3_out_4);  // AND_Gate
  and and_6 (and_6_out, sr_latch_1_out_4, sr_latch_2_out_4, button_1_out, ~sr_latch_3_out_4);  // AND_Gate
  SR_Latch sr_latch_1 (.R(and_1_out), .S(and_2_out), .POR(lul_out), .out_4(sr_latch_1_out_4));
  SR_Latch sr_latch_2 (.R(and_3_out), .S(and_4_out), .POR(lul_out), .out_4(sr_latch_2_out_4));
  SR_Latch sr_latch_3 (.R(and_5_out), .S(and_6_out), .POR(lul_out), .out_4(sr_latch_3_out_4));
  LED led_1 (.in(sr_latch_1_out_4));
  LED led_2 (.in(sr_latch_2_out_4));
  LED led_3 (.in(sr_latch_3_out_4));
endmodule

module DFlip_Flop (
  input  D,
  input  E,
  output Q
);

  wire not_1_out, not_2_out, Qm;

  not not_1 (not_1_out, E);
  // D_Latch Master: pin names not known; wires that end beside it: Qm
  not not_2 (not_2_out, not_1_out);
  // D_Latch Slave: pin names not known; wires that end beside it: Q

  // Other names for the same wires on the sheet: Qs = Q
endmodule

module SR_Latch (
  input  R,
  input  S,
  input  POR,
  output out_4
);

  wire nor_2_out, or_1_out;

  or or_1 (or_1_out, S, POR);
  nor nor_1 (out_4, R, nor_2_out);
  nor nor_2 (nor_2_out, out_4, or_1_out);
endmodule

module test (
  input  R,
  input  S,
  output Q
);

  or or_1 (Q, S, R);
endmodule
