// Logisim project TP_2.2.circ as structural Verilog: 4 circuits, main circuit D_Latch
module D_Latch (
  input  D,
  input  E,
  output Q
);

  wire nand_1_out, nand_2_out, nand_4_out;

  nand nand_1 (nand_1_out, D, E);
  nand nand_2 (nand_2_out, nand_1_out, E);
  nand nand_3 (Q, nand_1_out, nand_4_out);
  nand nand_4 (nand_4_out, Q, nand_2_out);
endmodule

module D_FlipFlop (
  input  D,
  input  E,
  output Q
);

  wire not_1_out, not_2_out, Qm;

  not not_1 (not_1_out, E);
  D_Latch Master (.D(D), .E(not_1_out), .Q(Qm));
  not not_2 (not_2_out, not_1_out);
  D_Latch Slave (.D(Qm), .E(not_2_out), .Q(Q));

  // Other names for the same wires on the sheet: Qs = Q
endmodule

module main (
  input  in_1,
  input  D,
  output out_3,
  output out_4
);

  wire E_out, not_1_out;

  Button E (.out(E_out));
  not not_1 (not_1_out, E_out);
  D_Latch d_latch_1 (.D(D), .E(E_out), .Q(out_4));
  LED led_1 (.in(out_4));
  LED led_2 (.in(not_1_out));
  SR_Latch sr_latch_1 (.out_1(out_3));
endmodule

module SR_Latch (
  output out_1
);

  wire nor_2_out, R_out, S_out;

  Button R (.out(R_out));
  Button S (.out(S_out));
  nor nor_1 (out_1, R_out, nor_2_out);
  nor nor_2 (nor_2_out, out_1, S_out);
endmodule
