// Logisim project tp34.circ as structural Verilog: 17 circuits, main circuit TP34_StudentSolution
module TP34 (
);

  wire But_out, clk_out, reset_out, StudentSol_disp0a, StudentSol_disp0b, StudentSol_disp0c,
       StudentSol_disp0d, StudentSol_disp0e, StudentSol_disp0f, StudentSol_disp0g, StudentSol_disp0point,
       StudentSol_disp1a, StudentSol_disp1b, StudentSol_disp1c, StudentSol_disp1d, StudentSol_disp1e,
       StudentSol_disp1f, StudentSol_disp1g, StudentSol_disp1point, StudentSol_disp2a, StudentSol_disp2b,
       StudentSol_disp2c, StudentSol_disp2d, StudentSol_disp2e, StudentSol_disp2f, StudentSol_disp2g,
       StudentSol_disp2point, StudentSol_q00, StudentSol_q01, StudentSol_q02, StudentSol_q10, StudentSol_q11,
       StudentSol_q12, StudentSol_q20, StudentSol_q21, StudentSol_q22;

  Button But (.out(But_out));
  Clock clk (.out(clk_out));
  Button reset (.out(reset_out));
  _7_Segment_Display Disp2 (
    .g(StudentSol_disp2g), .f(StudentSol_disp2f), .a(StudentSol_disp2a), .b(StudentSol_disp2b),
    .e(StudentSol_disp2e), .d(StudentSol_disp2d), .c(StudentSol_disp2c), .dp(StudentSol_disp2point));
  _7_Segment_Display Disp1 (
    .g(StudentSol_disp1g), .f(StudentSol_disp1f), .a(StudentSol_disp1a), .b(StudentSol_disp1b),
    .e(StudentSol_disp1e), .d(StudentSol_disp1d), .c(StudentSol_disp1c), .dp(StudentSol_disp1point));
  LED Q22 (.in(StudentSol_q22));
  LED Q12 (.in(StudentSol_q12));
  LED Q02 (.in(StudentSol_q02));
  _7_Segment_Display Disp0 (
    .g(StudentSol_disp0g), .f(StudentSol_disp0f), .a(StudentSol_disp0a), .b(StudentSol_disp0b),
    .e(StudentSol_disp0e), .d(StudentSol_disp0d), .c(StudentSol_disp0c), .dp(StudentSol_disp0point));
  LED Q21 (.in(StudentSol_q21));
  LED Q20 (.in(StudentSol_q20));
  LED Q11 (.in(StudentSol_q11));
  LED Q10 (.in(StudentSol_q10));
  LED Q01 (.in(StudentSol_q01));
  LED Q00 (.in(StudentSol_q00));
  TP34_StudentSolution StudentSol (
    .Disp0D(StudentSol_disp0d), .Disp0E(StudentSol_disp0e), .Disp0F(StudentSol_disp0f),
    .Disp0G(StudentSol_disp0g), .Disp0Point(StudentSol_disp0point), .Q00(StudentSol_q00),
    .Q01(StudentSol_q01), .Q02(StudentSol_q02), .Disp0A(StudentSol_disp0a), .Disp0B(StudentSol_disp0b),
    .Disp0C(StudentSol_disp0c), .Disp1D(StudentSol_disp1d), .Disp1E(StudentSol_disp1e),
    .Disp1F(StudentSol_disp1f), .Disp1G(StudentSol_disp1g), .Disp1Point(StudentSol_disp1point),
    .Q10(StudentSol_q10), .Q11(StudentSol_q11), .Q12(StudentSol_q12), .Disp1A(StudentSol_disp1a),
    .Disp1B(StudentSol_disp1b), .Disp1C(StudentSol_disp1c), .Disp2D(StudentSol_disp2d),
    .Disp2E(StudentSol_disp2e), .Disp2F(StudentSol_disp2f), .Disp2G(StudentSol_disp2g),
    .Disp2Point(StudentSol_disp2point), .Q20(StudentSol_q20), .Q21(StudentSol_q21), .Q22(StudentSol_q22),
    .Disp2A(StudentSol_disp2a), .Disp2B(StudentSol_disp2b), .Disp2C(StudentSol_disp2c), .res(reset_out),
    .But(But_out), .clk(clk_out));
endmodule

module TP34_StudentSolution (
  input  But,
  input  clk,
  input  res,
  output Disp0A,
  output Disp1A,
  output Disp2A,
  output Disp0B,
  output Disp1B,
  output Disp2B,
  output Disp0C,
  output Disp1C,
  output Disp2C,
  output Disp0D,
  output Disp1D,
  output Disp2D,
  output Disp0E,
  output Disp1E,
  output Disp2E,
  output Disp0F,
  output Disp1F,
  output Disp2F,
  output Disp0G,
  output Disp1G,
  output Disp2G,
  output Disp0Point,
  output Disp1Point,
  output Disp2Point,
  output Q00,
  output Q10,
  output Q20,
  output Q01,
  output Q11,
  output Q21,
  output Q02,
  output Q12,
  output Q22
);

  Base5_3Counters Base5_3Counters_1 (
    .Clock(clk), .Btn(1'b1), .Reset(res), .Q0({Q02, Q01, Q00}),
    .Disp0({Disp0Point, Disp0G, Disp0F, Disp0E, Disp0D, Disp0C, Disp0B, Disp0A}), .Q1({Q12, Q11, Q10}),
    .Disp1({Disp1Point, Disp1G, Disp1F, Disp1E, Disp1D, Disp1C, Disp1B, Disp1A}), .Q2({Q22, Q21, Q20}),
    .Disp2({Disp2Point, Disp2G, Disp2F, Disp2E, Disp2D, Disp2C, Disp2B, Disp2A}));

  // Other names for the same wires on the sheet: Button = But; Clock = clk;
  //   Disp0[7:0] = {Disp0Point, Disp0G, Disp0F, Disp0E, Disp0D, Disp0C, Disp0B, Disp0A};
  //   Disp1[7:0] = {Disp1Point, Disp1G, Disp1F, Disp1E, Disp1D, Disp1C, Disp1B, Disp1A};
  //   Disp2[7:0] = {Disp2Point, Disp2G, Disp2F, Disp2E, Disp2D, Disp2C, Disp2B, Disp2A}; Reset = res

  // Notes on the sheet:
  //   Disp0
  //   Q0
  //   Disp1
  //   Q1
  //   Q2
  //   Disp2
endmodule

module TP34Q1Video (
);

  wire clock_1_out, StudentSol_disp0a, StudentSol_disp0b, StudentSol_disp0c, StudentSol_disp0d,
       StudentSol_disp0e, StudentSol_disp0f, StudentSol_disp0g, StudentSol_disp0point, StudentSol_disp1a,
       StudentSol_disp1b, StudentSol_disp1c, StudentSol_disp1d, StudentSol_disp1e, StudentSol_disp1f,
       StudentSol_disp1g, StudentSol_disp1point, StudentSol_disp2a, StudentSol_disp2b, StudentSol_disp2c,
       StudentSol_disp2d, StudentSol_disp2e, StudentSol_disp2f, StudentSol_disp2g, StudentSol_disp2point,
       StudentSol_q00, StudentSol_q01, StudentSol_q02, StudentSol_q10, StudentSol_q11, StudentSol_q12,
       StudentSol_q20, StudentSol_q21, StudentSol_q22, undriven, undriven_2;
  wire [9:0] counter_1_q;

  Clock clock_1 (.out(clock_1_out));
  ROM #(.addrWidth(10), .dataWidth(1)) ROM_But_Q1_sg (.addr(counter_1_q));  // open: data
  Counter #(.max('h187), .width(10)) counter_1 (
    .clr(1'b0), .load(1'b0), .up(1'b1), .count(1'b1), .clk(clock_1_out), .D({10{1'b0}}), .Q(counter_1_q));  // open: carry
  ROM #(.addrWidth(10), .dataWidth(1)) ROM_reset_sg (.addr(counter_1_q));  // open: data
  _7_Segment_Display Disp2 (
    .g(StudentSol_disp2g), .f(StudentSol_disp2f), .a(StudentSol_disp2a), .b(StudentSol_disp2b),
    .e(StudentSol_disp2e), .d(StudentSol_disp2d), .c(StudentSol_disp2c), .dp(StudentSol_disp2point));
  _7_Segment_Display Disp1 (
    .g(StudentSol_disp1g), .f(StudentSol_disp1f), .a(StudentSol_disp1a), .b(StudentSol_disp1b),
    .e(StudentSol_disp1e), .d(StudentSol_disp1d), .c(StudentSol_disp1c), .dp(StudentSol_disp1point));
  LED Q22 (.in(StudentSol_q22));
  LED Q21 (.in(StudentSol_q21));
  LED Q12 (.in(StudentSol_q12));
  LED Q11 (.in(StudentSol_q11));
  LED Q02 (.in(StudentSol_q02));
  LED Q01 (.in(StudentSol_q01));
  _7_Segment_Display Disp0 (
    .g(StudentSol_disp0g), .f(StudentSol_disp0f), .a(StudentSol_disp0a), .b(StudentSol_disp0b),
    .e(StudentSol_disp0e), .d(StudentSol_disp0d), .c(StudentSol_disp0c), .dp(StudentSol_disp0point));
  LED Q20 (.in(StudentSol_q20));
  LED Q10 (.in(StudentSol_q10));
  LED Q00 (.in(StudentSol_q00));
  TP34_StudentSolution StudentSol (
    .Disp0D(StudentSol_disp0d), .Disp0E(StudentSol_disp0e), .Disp0F(StudentSol_disp0f),
    .Disp0G(StudentSol_disp0g), .Disp0Point(StudentSol_disp0point), .Q00(StudentSol_q00),
    .Q01(StudentSol_q01), .Q02(StudentSol_q02), .Disp0A(StudentSol_disp0a), .Disp0B(StudentSol_disp0b),
    .Disp0C(StudentSol_disp0c), .Disp1D(StudentSol_disp1d), .Disp1E(StudentSol_disp1e),
    .Disp1F(StudentSol_disp1f), .Disp1G(StudentSol_disp1g), .Disp1Point(StudentSol_disp1point),
    .Q10(StudentSol_q10), .Q11(StudentSol_q11), .Q12(StudentSol_q12), .Disp1A(StudentSol_disp1a),
    .Disp1B(StudentSol_disp1b), .Disp1C(StudentSol_disp1c), .Disp2D(StudentSol_disp2d),
    .Disp2E(StudentSol_disp2e), .Disp2F(StudentSol_disp2f), .Disp2G(StudentSol_disp2g),
    .Disp2Point(StudentSol_disp2point), .Q20(StudentSol_q20), .Q21(StudentSol_q21), .Q22(StudentSol_q22),
    .Disp2A(StudentSol_disp2a), .Disp2B(StudentSol_disp2b), .Disp2C(StudentSol_disp2c), .res(undriven_2),
    .But(undriven), .clk(clock_1_out));

  // Notes on the sheet:
  //   contents of ROM_reset_sg (hex, n*v repeats v):
  //   5*1
endmodule

module TP34Q2Video (
);

  wire clock_1_out, StudentSol_disp0a, StudentSol_disp0b, StudentSol_disp0c, StudentSol_disp0d,
       StudentSol_disp0e, StudentSol_disp0f, StudentSol_disp0g, StudentSol_disp0point, StudentSol_disp1a,
       StudentSol_disp1b, StudentSol_disp1c, StudentSol_disp1d, StudentSol_disp1e, StudentSol_disp1f,
       StudentSol_disp1g, StudentSol_disp1point, StudentSol_disp2a, StudentSol_disp2b, StudentSol_disp2c,
       StudentSol_disp2d, StudentSol_disp2e, StudentSol_disp2f, StudentSol_disp2g, StudentSol_disp2point,
       StudentSol_q00, StudentSol_q01, StudentSol_q02, StudentSol_q10, StudentSol_q11, StudentSol_q12,
       StudentSol_q20, StudentSol_q21, StudentSol_q22, undriven, undriven_2;
  wire [9:0] counter_1_q;

  Clock clock_1 (.out(clock_1_out));
  ROM #(.addrWidth(10), .dataWidth(1)) ROM_But_Q1_sg (.addr(counter_1_q));  // open: data
  Counter #(.max('h187), .width(10)) counter_1 (
    .clr(1'b0), .load(1'b0), .up(1'b1), .count(1'b1), .clk(clock_1_out), .D({10{1'b0}}), .Q(counter_1_q));  // open: carry
  ROM #(.addrWidth(10), .dataWidth(1)) ROM_reset_sg (.addr(counter_1_q));  // open: data
  _7_Segment_Display Disp2 (
    .g(StudentSol_disp2g), .f(StudentSol_disp2f), .a(StudentSol_disp2a), .b(StudentSol_disp2b),
    .e(StudentSol_disp2e), .d(StudentSol_disp2d), .c(StudentSol_disp2c), .dp(StudentSol_disp2point));
  _7_Segment_Display Disp1 (
    .g(StudentSol_disp1g), .f(StudentSol_disp1f), .a(StudentSol_disp1a), .b(StudentSol_disp1b),
    .e(StudentSol_disp1e), .d(StudentSol_disp1d), .c(StudentSol_disp1c), .dp(StudentSol_disp1point));
  LED Q22 (.in(StudentSol_q22));
  LED Q21 (.in(StudentSol_q21));
  LED Q12 (.in(StudentSol_q12));
  LED Q11 (.in(StudentSol_q11));
  LED Q02 (.in(StudentSol_q02));
  LED Q01 (.in(StudentSol_q01));
  _7_Segment_Display Disp0 (
    .g(StudentSol_disp0g), .f(StudentSol_disp0f), .a(StudentSol_disp0a), .b(StudentSol_disp0b),
    .e(StudentSol_disp0e), .d(StudentSol_disp0d), .c(StudentSol_disp0c), .dp(StudentSol_disp0point));
  LED Q20 (.in(StudentSol_q20));
  LED Q10 (.in(StudentSol_q10));
  LED Q00 (.in(StudentSol_q00));
  TP34_StudentSolution StudentSol (
    .Disp0D(StudentSol_disp0d), .Disp0E(StudentSol_disp0e), .Disp0F(StudentSol_disp0f),
    .Disp0G(StudentSol_disp0g), .Disp0Point(StudentSol_disp0point), .Q00(StudentSol_q00),
    .Q01(StudentSol_q01), .Q02(StudentSol_q02), .Disp0A(StudentSol_disp0a), .Disp0B(StudentSol_disp0b),
    .Disp0C(StudentSol_disp0c), .Disp1D(StudentSol_disp1d), .Disp1E(StudentSol_disp1e),
    .Disp1F(StudentSol_disp1f), .Disp1G(StudentSol_disp1g), .Disp1Point(StudentSol_disp1point),
    .Q10(StudentSol_q10), .Q11(StudentSol_q11), .Q12(StudentSol_q12), .Disp1A(StudentSol_disp1a),
    .Disp1B(StudentSol_disp1b), .Disp1C(StudentSol_disp1c), .Disp2D(StudentSol_disp2d),
    .Disp2E(StudentSol_disp2e), .Disp2F(StudentSol_disp2f), .Disp2G(StudentSol_disp2g),
    .Disp2Point(StudentSol_disp2point), .Q20(StudentSol_q20), .Q21(StudentSol_q21), .Q22(StudentSol_q22),
    .Disp2A(StudentSol_disp2a), .Disp2B(StudentSol_disp2b), .Disp2C(StudentSol_disp2c), .res(undriven_2),
    .But(undriven), .clk(clock_1_out));

  // Notes on the sheet:
  //   contents of ROM_But_Q1_sg (hex, n*v repeats v):
  //   131*0 1 126*0 1
  //   contents of ROM_reset_sg (hex, n*v repeats v):
  //   5*1
endmodule

module TP34Q3Video (
);

  wire clock_1_out, StudentSol_disp0a, StudentSol_disp0b, StudentSol_disp0c, StudentSol_disp0d,
       StudentSol_disp0e, StudentSol_disp0f, StudentSol_disp0g, StudentSol_disp0point, StudentSol_disp1a,
       StudentSol_disp1b, StudentSol_disp1c, StudentSol_disp1d, StudentSol_disp1e, StudentSol_disp1f,
       StudentSol_disp1g, StudentSol_disp1point, StudentSol_disp2a, StudentSol_disp2b, StudentSol_disp2c,
       StudentSol_disp2d, StudentSol_disp2e, StudentSol_disp2f, StudentSol_disp2g, StudentSol_disp2point,
       StudentSol_q00, StudentSol_q01, StudentSol_q02, StudentSol_q10, StudentSol_q11, StudentSol_q12,
       StudentSol_q20, StudentSol_q21, StudentSol_q22, undriven, undriven_2;
  wire [9:0] counter_1_q;

  Clock clock_1 (.out(clock_1_out));
  ROM #(.addrWidth(10), .dataWidth(1)) ROM_But_Q1_sg (.addr(counter_1_q));  // open: data
  Counter #(.max('h187), .width(10)) counter_1 (
    .clr(1'b0), .load(1'b0), .up(1'b1), .count(1'b1), .clk(clock_1_out), .D({10{1'b0}}), .Q(counter_1_q));  // open: carry
  ROM #(.addrWidth(10), .dataWidth(1)) ROM_reset_sg (.addr(counter_1_q));  // open: data
  _7_Segment_Display Disp2 (
    .g(StudentSol_disp2g), .f(StudentSol_disp2f), .a(StudentSol_disp2a), .b(StudentSol_disp2b),
    .e(StudentSol_disp2e), .d(StudentSol_disp2d), .c(StudentSol_disp2c), .dp(StudentSol_disp2point));
  _7_Segment_Display Disp1 (
    .g(StudentSol_disp1g), .f(StudentSol_disp1f), .a(StudentSol_disp1a), .b(StudentSol_disp1b),
    .e(StudentSol_disp1e), .d(StudentSol_disp1d), .c(StudentSol_disp1c), .dp(StudentSol_disp1point));
  LED Q22 (.in(StudentSol_q22));
  LED Q21 (.in(StudentSol_q21));
  LED Q12 (.in(StudentSol_q12));
  LED Q11 (.in(StudentSol_q11));
  LED Q02 (.in(StudentSol_q02));
  LED Q01 (.in(StudentSol_q01));
  _7_Segment_Display Disp0 (
    .g(StudentSol_disp0g), .f(StudentSol_disp0f), .a(StudentSol_disp0a), .b(StudentSol_disp0b),
    .e(StudentSol_disp0e), .d(StudentSol_disp0d), .c(StudentSol_disp0c), .dp(StudentSol_disp0point));
  LED Q20 (.in(StudentSol_q20));
  LED Q10 (.in(StudentSol_q10));
  LED Q00 (.in(StudentSol_q00));
  TP34_StudentSolution StudentSol (
    .Disp0D(StudentSol_disp0d), .Disp0E(StudentSol_disp0e), .Disp0F(StudentSol_disp0f),
    .Disp0G(StudentSol_disp0g), .Disp0Point(StudentSol_disp0point), .Q00(StudentSol_q00),
    .Q01(StudentSol_q01), .Q02(StudentSol_q02), .Disp0A(StudentSol_disp0a), .Disp0B(StudentSol_disp0b),
    .Disp0C(StudentSol_disp0c), .Disp1D(StudentSol_disp1d), .Disp1E(StudentSol_disp1e),
    .Disp1F(StudentSol_disp1f), .Disp1G(StudentSol_disp1g), .Disp1Point(StudentSol_disp1point),
    .Q10(StudentSol_q10), .Q11(StudentSol_q11), .Q12(StudentSol_q12), .Disp1A(StudentSol_disp1a),
    .Disp1B(StudentSol_disp1b), .Disp1C(StudentSol_disp1c), .Disp2D(StudentSol_disp2d),
    .Disp2E(StudentSol_disp2e), .Disp2F(StudentSol_disp2f), .Disp2G(StudentSol_disp2g),
    .Disp2Point(StudentSol_disp2point), .Q20(StudentSol_q20), .Q21(StudentSol_q21), .Q22(StudentSol_q22),
    .Disp2A(StudentSol_disp2a), .Disp2B(StudentSol_disp2b), .Disp2C(StudentSol_disp2c), .res(undriven_2),
    .But(undriven), .clk(clock_1_out));

  // Notes on the sheet:
  //   contents of ROM_But_Q1_sg (hex, n*v repeats v):
  //   131*0 1 126*0 1
  //   contents of ROM_reset_sg (hex, n*v repeats v):
  //   5*1
endmodule

module CodeToDisp (
  input  [2:0] A_B_C,
  output [7:0] Q
);

  wire and_3_out, and_4_out, not_1_out, not_2_out, not_3_out;

  not not_1 (not_1_out, A_B_C[2]);
  not not_2 (not_2_out, A_B_C[1]);
  not not_3 (not_3_out, A_B_C[0]);
  or or_1 (Q[6], not_2_out, A_B_C[0]);
  and and_1 (Q[5], A_B_C[2], not_3_out);
  and and_2 (Q[4], A_B_C[2], A_B_C[1]);
  or or_2 (Q[3], A_B_C[0], and_3_out);
  and and_3 (and_3_out, A_B_C[2], A_B_C[1]);
  or or_3 (Q[2], not_1_out, not_3_out);
  or or_4 (Q[0], A_B_C[0], and_4_out);
  and and_4 (and_4_out, A_B_C[2], A_B_C[1]);

  assign {Q[7], Q[1]} = 2'b01;
endmodule

module binaryToCode (
  input  [2:0] I012,
  output [2:0] C012
);

  wire and_1_out, and_2_out, not_1_out, not_2_out;

  not not_1 (not_1_out, I012[2]);
  not not_2 (not_2_out, I012[1]);
  not not_3 (C012[2], I012[0]);
  and and_1 (and_1_out, not_1_out, not_2_out);
  and and_2 (and_2_out, not_1_out, C012[2]);
  or or_1 (C012[1], and_1_out, and_2_out);

  assign C012[0] = I012[1];
endmodule

module if_gate (
  input  A,
  input  Test,
  input  B,
  output P
);

  wire and_1_out, and_2_out;

  and and_1 (and_1_out, A, Test);
  and and_2 (and_2_out, ~Test, B);  // AND_Gate
  or or_1 (P, and_1_out, and_2_out);
endmodule

module if_3 (
  input  [2:0] A,
  input  Test,
  input  [2:0] B,
  output [2:0] P
);

  if_gate if_gate_1 (.A(A[0]), .Test(Test), .B(B[0]), .P(P[0]));
  if_gate if_gate_2 (.A(A[1]), .Test(Test), .B(B[1]), .P(P[1]));
  if_gate if_gate_3 (.A(A[2]), .Test(Test), .B(B[2]), .P(P[2]));
endmodule

module toRightOrder (
  input  [7:0] I,
  output [7:0] O
);


  assign O = {I[0], I[1], I[2], I[3], I[4], I[5], I[6], I[7]};
endmodule

module DFF_3 (
  input  [2:0] D,
  input  Clock,
  output [2:0] Q
);

  wire D0_qn, D2_qn;

  D_Flip_Flop D0 (.D(D[0]), .clk(Clock), .Q(Q[0]), .Qn(D0_qn));  // open: preset, reset
  D_Flip_Flop D1 (.D(D[1]), .clk(Clock), .Q(Q[1]));  // open: Qn, preset, reset
  D_Flip_Flop D2 (.D(D[2]), .clk(Clock), .Q(Q[2]), .Qn(D2_qn));  // open: preset, reset
  // NoConnect on D0_qn
  // NoConnect on D2_qn
endmodule

module Add (
  input  [2:0] B0,
  input  carry_in,
  output [2:0] B1,
  output Carry_out
);

  wire and_1_out, and_2_out, and_3_out, and_4_out, and_5_out, and_6_out, and_7_out, not_1_out, not_2_out,
       not_3_out, not_4_out;

  not not_1 (not_1_out, B0[2]);
  not not_2 (not_2_out, B0[1]);
  not not_3 (not_3_out, B0[0]);
  not not_4 (not_4_out, carry_in);
  and and_1 (and_1_out, not_4_out, B0[2]);
  and and_2 (and_2_out, carry_in, B0[1], B0[0]);
  and and_3 (and_3_out, not_4_out, B0[1]);
  and and_4 (and_4_out, B0[1], not_3_out);
  and and_5 (and_5_out, carry_in, not_1_out, not_2_out, B0[0]);
  and and_6 (and_6_out, not_4_out, B0[0]);
  and and_7 (and_7_out, carry_in, not_1_out, not_3_out);
  and and_8 (Carry_out, carry_in, B0[2]);
  or or_1 (B1[2], and_1_out, and_2_out);
  or or_2 (B1[1], and_3_out, and_4_out, and_5_out);
  or or_3 (B1[0], and_6_out, and_7_out);
endmodule

module Sub (
  input  [2:0] B0,
  input  carry_in,
  output [2:0] B1,
  output Carry_out
);

  wire and_1_out, and_2_out, and_3_out, and_4_out, and_5_out, and_6_out, and_7_out, and_8_out, not_1_out,
       not_2_out, not_3_out, not_4_out;

  not not_1 (not_1_out, B0[2]);
  not not_2 (not_2_out, B0[1]);
  not not_3 (not_3_out, B0[0]);
  not not_4 (not_4_out, carry_in);
  and and_1 (and_1_out, not_4_out, B0[2]);
  and and_2 (and_2_out, carry_in, not_1_out, not_2_out, not_3_out);
  and and_3 (and_3_out, not_4_out, B0[1]);
  and and_4 (and_4_out, B0[1], B0[0]);
  and and_5 (and_5_out, carry_in, B0[2]);
  and and_6 (and_6_out, not_4_out, B0[0]);
  and and_7 (and_7_out, carry_in, B0[1], not_3_out);
  and and_8 (and_8_out, carry_in, B0[2]);
  and and_9 (Carry_out, carry_in, not_1_out, not_2_out, not_3_out);
  or or_1 (B1[2], and_1_out, and_2_out);
  or or_2 (B1[1], and_3_out, and_4_out, and_5_out);
  or or_3 (B1[0], and_6_out, and_7_out, and_8_out);
endmodule

module Full_Counter (
  input  [2:0] C,
  input  Carry_in,
  input  Btn,
  output [2:0] D,
  output Cout
);

  wire Add_1_carry_out, Sub_1_carry_out;
  wire [2:0] Add_1_b1, Sub_1_b1;

  Add Add_1 (.B0(C), .carry_in(Carry_in), .B1(Add_1_b1), .Carry_out(Add_1_carry_out));
  Sub Sub_1 (.B0(C), .carry_in(Carry_in), .B1(Sub_1_b1), .Carry_out(Sub_1_carry_out));
  if_3 if_3_1 (.A(Add_1_b1), .Test(Btn), .B(Sub_1_b1), .P(D));
  if_gate if_gate_1 (.A(Add_1_carry_out), .Test(Btn), .B(Sub_1_carry_out), .P(Cout));
endmodule

// Disp2_FSM
module Base5_3Counters (
  input  Clock,
  input  Btn,
  input  Reset,
  output [2:0] Q0,
  output [7:0] Disp0,
  output [2:0] Q1,
  output [7:0] Disp1,
  output [2:0] Q2,
  output [7:0] Disp2
);

  wire Disp0_FSM_cout, Disp1_FSM_cout;

  Moore_FSM Disp0_FSM (
    .Cout(Disp0_FSM_cout), .Q(Q0), .Disp(Disp0), .Cin(1'b1), .Reset(Reset), .Btn(Btn), .Clock(Clock),
    .resetVal(3'b000));  // open: C, D, ValueForReset
  Moore_FSM Disp1_FSM (
    .Cout(Disp1_FSM_cout), .Q(Q1), .Disp(Disp1), .Cin(Disp0_FSM_cout), .Reset(Reset), .Btn(Btn),
    .Clock(Clock), .resetVal(3'b001));  // open: C, D, ValueForReset
  Moore_FSM Disp2_FSM (
    .Q(Q2), .Disp(Disp2), .Cin(Disp1_FSM_cout), .Reset(Reset), .Btn(Btn), .Clock(Clock), .resetVal(3'b010));  // open: C, D, Cout, ValueForReset
endmodule

module BinToCdToDisp (
  input  [2:0] C,
  output [2:0] Q,
  output [7:0] Disp
);

  binaryToCode binaryToCode_1 (.I012(C), .C012(Q));
  CodeToDisp CodeToDisp_1 (.A_B_C(Q), .Q(Disp));
endmodule

module Moore_FSM (
  input  Clock,
  input  Cin,
  input  Reset,
  input  [2:0] resetVal,
  input  Btn,
  output [2:0] C,
  output [2:0] D,
  output [2:0] Q,
  output [7:0] Disp,
  output Cout,
  output [2:0] ValueForReset
);

  wire and_1_out;
  wire [2:0] if_3_1_p;

  and and_1 (and_1_out, Cin, ~Reset);  // AND_Gate
  Full_Counter Transition_logic (.C(C), .Carry_in(and_1_out), .Btn(Btn), .D(D), .Cout(Cout));
  if_3 if_3_1 (.A(resetVal), .Test(Reset), .B(D), .P(if_3_1_p));
  DFF_3 DFF_3_1 (.Q(C), .D(if_3_1_p), .Clock(Clock));
  BinToCdToDisp Output_Logic (.C(C), .Q(Q), .Disp(Disp));

  assign ValueForReset = resetVal;

  // Other names for the same wires on the sheet: v[2:0] = resetVal
endmodule
