// Logisim project toplevel.circ as structural Verilog: 6 circuits, main circuit transition_logic
module laboratory6_top (
  input  n_reset,
  input  clock,
  output LED
);

  wire s_kick_ass, s_reset;

  not not_1 (s_reset, n_reset);
  clock_divider clock_div (.reset(s_reset), .clock(clock), .enable(s_kick_ass));
  tff_sr blinker (.T(s_kick_ass), .reset(s_reset), .clock(clock), .LED(LED));

  // Other names for the same wires on the sheet: s_50MHz_clock = clock; s_the_blinking_light = LED
endmodule

module transition_logic (
);

  wire comparator_1_eq;
  wire [24:0] s_current_state, s_next_state, subtractor_1_out;

  Subtractor #(.width(25)) subtractor_1 (.a(s_current_state), .b(25'h1), .out(subtractor_1_out));  // open: bin, bout
  Comparator #(.mode("unsigned"), .width(25)) comparator_1 (
    .a(s_current_state), .b({25{1'b0}}), .eq(comparator_1_eq));  // open: gt, lt
  Multiplexer #(.enable("false"), .width(25)) multiplexer_1 (
    .in0(subtractor_1_out), .in1(25'h17d783f), .out(s_next_state), .sel(comparator_1_eq));

  // Notes on the sheet:
  //   c_reload_value
endmodule

module flipflops (
  input  reset,
  input  clock
);

  wire [24:0] multiplexer_1_out, s_current_state, s_next_state;

  Multiplexer #(.enable("false"), .width(25)) multiplexer_1 (
    .in0(s_next_state), .in1({25{1'b0}}), .out(multiplexer_1_out), .sel(reset));
  D_Flip_Flop d_ff_1 (.D(multiplexer_1_out[4]), .clk(clock), .Q(s_current_state[4]));  // open: Qn, preset, reset
  D_Flip_Flop d_ff_2 (.D(multiplexer_1_out[9]), .clk(clock), .Q(s_current_state[9]));  // open: Qn, preset, reset
  D_Flip_Flop d_ff_3 (.D(multiplexer_1_out[14]), .clk(clock), .Q(s_current_state[14]));  // open: Qn, preset, reset
  D_Flip_Flop d_ff_4 (.D(multiplexer_1_out[19]), .clk(clock), .Q(s_current_state[19]));  // open: Qn, preset, reset
  D_Flip_Flop d_ff_5 (.D(multiplexer_1_out[24]), .clk(clock), .Q(s_current_state[24]));  // open: Qn, preset, reset
  D_Flip_Flop d_ff_6 (.D(multiplexer_1_out[3]), .clk(clock), .Q(s_current_state[3]));  // open: Qn, preset, reset
  D_Flip_Flop d_ff_7 (.D(multiplexer_1_out[8]), .clk(clock), .Q(s_current_state[8]));  // open: Qn, preset, reset
  D_Flip_Flop d_ff_8 (.D(multiplexer_1_out[13]), .clk(clock), .Q(s_current_state[13]));  // open: Qn, preset, reset
  D_Flip_Flop d_ff_9 (.D(multiplexer_1_out[18]), .clk(clock), .Q(s_current_state[18]));  // open: Qn, preset, reset
  D_Flip_Flop d_ff_10 (.D(multiplexer_1_out[23]), .clk(clock), .Q(s_current_state[23]));  // open: Qn, preset, reset
  D_Flip_Flop d_ff_11 (.D(multiplexer_1_out[2]), .clk(clock), .Q(s_current_state[2]));  // open: Qn, preset, reset
  D_Flip_Flop d_ff_12 (.D(multiplexer_1_out[7]), .clk(clock), .Q(s_current_state[7]));  // open: Qn, preset, reset
  D_Flip_Flop d_ff_13 (.D(multiplexer_1_out[12]), .clk(clock), .Q(s_current_state[12]));  // open: Qn, preset, reset
  D_Flip_Flop d_ff_14 (.D(multiplexer_1_out[17]), .clk(clock), .Q(s_current_state[17]));  // open: Qn, preset, reset
  D_Flip_Flop d_ff_15 (.D(multiplexer_1_out[22]), .clk(clock), .Q(s_current_state[22]));  // open: Qn, preset, reset
  D_Flip_Flop d_ff_16 (.D(multiplexer_1_out[1]), .clk(clock), .Q(s_current_state[1]));  // open: Qn, preset, reset
  D_Flip_Flop d_ff_17 (.D(multiplexer_1_out[6]), .clk(clock), .Q(s_current_state[6]));  // open: Qn, preset, reset
  D_Flip_Flop d_ff_18 (.D(multiplexer_1_out[11]), .clk(clock), .Q(s_current_state[11]));  // open: Qn, preset, reset
  D_Flip_Flop d_ff_19 (.D(multiplexer_1_out[16]), .clk(clock), .Q(s_current_state[16]));  // open: Qn, preset, reset
  D_Flip_Flop d_ff_20 (.D(multiplexer_1_out[21]), .clk(clock), .Q(s_current_state[21]));  // open: Qn, preset, reset
  D_Flip_Flop d_ff_21 (.D(multiplexer_1_out[0]), .clk(clock), .Q(s_current_state[0]));  // open: Qn, preset, reset
  D_Flip_Flop d_ff_22 (.D(multiplexer_1_out[5]), .clk(clock), .Q(s_current_state[5]));  // open: Qn, preset, reset
  D_Flip_Flop d_ff_23 (.D(multiplexer_1_out[10]), .clk(clock), .Q(s_current_state[10]));  // open: Qn, preset, reset
  D_Flip_Flop d_ff_24 (.D(multiplexer_1_out[15]), .clk(clock), .Q(s_current_state[15]));  // open: Qn, preset, reset
  D_Flip_Flop d_ff_25 (.D(multiplexer_1_out[20]), .clk(clock), .Q(s_current_state[20]));  // open: Qn, preset, reset
endmodule

module clock_divider (
  input  reset,
  input  clock,
  output enable
);

  wire comparator_1_eq, not_1_out;
  wire [24:0] multiplexer_2_out, s_current_state, s_next_state, subtractor_1_out;

  Subtractor #(.width(25)) subtractor_1 (.a(s_current_state), .b(25'h1), .out(subtractor_1_out));  // open: bin, bout
  Comparator #(.mode("unsigned"), .width(25)) comparator_1 (
    .a(s_current_state), .b({25{1'b0}}), .eq(comparator_1_eq));  // open: gt, lt
  Multiplexer #(.enable("false"), .width(25)) multiplexer_1 (
    .in0(subtractor_1_out), .in1(25'h17d783f), .out(s_next_state), .sel(comparator_1_eq));
  Multiplexer #(.enable("false"), .width(25)) multiplexer_2 (
    .in0(s_next_state), .in1({25{1'b0}}), .out(multiplexer_2_out), .sel(reset));
  D_Flip_Flop d_ff_1 (.D(multiplexer_2_out[4]), .clk(clock), .Q(s_current_state[4]));  // open: Qn, preset, reset
  D_Flip_Flop d_ff_2 (.D(multiplexer_2_out[9]), .clk(clock), .Q(s_current_state[9]));  // open: Qn, preset, reset
  D_Flip_Flop d_ff_3 (.D(multiplexer_2_out[14]), .clk(clock), .Q(s_current_state[14]));  // open: Qn, preset, reset
  D_Flip_Flop d_ff_4 (.D(multiplexer_2_out[19]), .clk(clock), .Q(s_current_state[19]));  // open: Qn, preset, reset
  D_Flip_Flop d_ff_5 (.D(multiplexer_2_out[24]), .clk(clock), .Q(s_current_state[24]));  // open: Qn, preset, reset
  D_Flip_Flop d_ff_6 (.D(multiplexer_2_out[3]), .clk(clock), .Q(s_current_state[3]));  // open: Qn, preset, reset
  D_Flip_Flop d_ff_7 (.D(multiplexer_2_out[8]), .clk(clock), .Q(s_current_state[8]));  // open: Qn, preset, reset
  D_Flip_Flop d_ff_8 (.D(multiplexer_2_out[13]), .clk(clock), .Q(s_current_state[13]));  // open: Qn, preset, reset
  D_Flip_Flop d_ff_9 (.D(multiplexer_2_out[18]), .clk(clock), .Q(s_current_state[18]));  // open: Qn, preset, reset
  D_Flip_Flop d_ff_10 (.D(multiplexer_2_out[23]), .clk(clock), .Q(s_current_state[23]));  // open: Qn, preset, reset
  D_Flip_Flop d_ff_11 (.D(multiplexer_2_out[2]), .clk(clock), .Q(s_current_state[2]));  // open: Qn, preset, reset
  D_Flip_Flop d_ff_12 (.D(multiplexer_2_out[7]), .clk(clock), .Q(s_current_state[7]));  // open: Qn, preset, reset
  D_Flip_Flop d_ff_13 (.D(multiplexer_2_out[12]), .clk(clock), .Q(s_current_state[12]));  // open: Qn, preset, reset
  D_Flip_Flop d_ff_14 (.D(multiplexer_2_out[17]), .clk(clock), .Q(s_current_state[17]));  // open: Qn, preset, reset
  D_Flip_Flop d_ff_15 (.D(multiplexer_2_out[22]), .clk(clock), .Q(s_current_state[22]));  // open: Qn, preset, reset
  D_Flip_Flop d_ff_16 (.D(multiplexer_2_out[1]), .clk(clock), .Q(s_current_state[1]));  // open: Qn, preset, reset
  D_Flip_Flop d_ff_17 (.D(multiplexer_2_out[6]), .clk(clock), .Q(s_current_state[6]));  // open: Qn, preset, reset
  D_Flip_Flop d_ff_18 (.D(multiplexer_2_out[11]), .clk(clock), .Q(s_current_state[11]));  // open: Qn, preset, reset
  D_Flip_Flop d_ff_19 (.D(multiplexer_2_out[16]), .clk(clock), .Q(s_current_state[16]));  // open: Qn, preset, reset
  D_Flip_Flop d_ff_20 (.D(multiplexer_2_out[21]), .clk(clock), .Q(s_current_state[21]));  // open: Qn, preset, reset
  D_Flip_Flop d_ff_21 (.D(multiplexer_2_out[0]), .clk(clock), .Q(s_current_state[0]));  // open: Qn, preset, reset
  D_Flip_Flop d_ff_22 (.D(multiplexer_2_out[5]), .clk(clock), .Q(s_current_state[5]));  // open: Qn, preset, reset
  D_Flip_Flop d_ff_23 (.D(multiplexer_2_out[10]), .clk(clock), .Q(s_current_state[10]));  // open: Qn, preset, reset
  D_Flip_Flop d_ff_24 (.D(multiplexer_2_out[15]), .clk(clock), .Q(s_current_state[15]));  // open: Qn, preset, reset
  D_Flip_Flop d_ff_25 (.D(multiplexer_2_out[20]), .clk(clock), .Q(s_current_state[20]));  // open: Qn, preset, reset
  not not_1 (not_1_out, s_current_state[0]);
  nor nor_1 (enable, not_1_out, s_current_state[1], s_current_state[2], s_current_state[3], s_current_state[4], s_current_state[5], s_current_state[6], s_current_state[7], s_current_state[8], s_current_state[9], s_current_state[10], s_current_state[11], s_current_state[12], s_current_state[13], s_current_state[14], s_current_state[15], s_current_state[16], s_current_state[17], s_current_state[18], s_current_state[19], s_current_state[20], s_current_state[21], s_current_state[22], s_current_state[23], s_current_state[24]);

  // Notes on the sheet:
  //   c_reload_value
endmodule

module output_logic (
  output enable,
  output enable1
);

  wire comparator_1_eq, not_1_out;
  wire [24:0] s_current_state;

  Multiplexer #(.enable("false")) multiplexer_1 (.in0(1'b0), .in1(1'b1), .out(enable), .sel(comparator_1_eq));
  Comparator #(.mode("unsigned"), .width(25)) comparator_1 (
    .a(s_current_state), .b(25'h1), .eq(comparator_1_eq));  // open: gt, lt
  not not_1 (not_1_out, s_current_state[0]);
  nor nor_1 (enable1, not_1_out, s_current_state[1], s_current_state[2], s_current_state[3], s_current_state[4], s_current_state[5], s_current_state[6], s_current_state[7], s_current_state[8], s_current_state[9], s_current_state[10], s_current_state[11], s_current_state[12], s_current_state[13], s_current_state[14], s_current_state[15], s_current_state[16], s_current_state[17], s_current_state[18], s_current_state[19], s_current_state[20], s_current_state[21], s_current_state[22], s_current_state[23], s_current_state[24]);

  // Notes on the sheet:
  //   OR:
endmodule

module tff_sr (
  input  T,
  input  reset,
  input  clock,
  output LED
);

  wire and_1_out, not_1_out, xor_1_out;

  xor xor_1 (xor_1_out, LED, T);
  not not_1 (not_1_out, reset);
  D_Flip_Flop d_ff_1 (.D(and_1_out), .clk(clock), .Q(LED));  // open: Qn, preset, reset
  and and_1 (and_1_out, xor_1_out, not_1_out);
endmodule
